// Logisim project Four_Bits_Add_Sub.circ as structural Verilog: 3 circuits, main circuit Add_Sub_4Bits
module Add_Sub_4Bits (
  input  [3:0] B,
  input  [3:0] A,
  input  Add_Sub,
  output [3:0] R,
  output Zero,
  output Overflow
);

  wire A0_z, A1_z, A2_z, A3_z, add_1bit_1_cout, add_1bit_1_sum, add_1bit_2_cout, add_1bit_2_sum,
       add_1bit_3_cout, add_1bit_3_sum, add_1bit_4_sum, add_1bit_5_cout, add_1bit_6_cout, add_1bit_7_cout,
       not_1_out, not_2_out, not_3_out, not_4_out, not_5_out;

  // Probe on B
  not not_1 (not_1_out, B[1]);
  not not_2 (not_2_out, B[2]);
  not not_3 (not_3_out, B[3]);
  not not_4 (not_4_out, B[0]);
  not not_5 (not_5_out, Add_Sub);
  My_Multiplexer A0 (.z(A0_z), .y(Add_Sub), .x_1(B[0]), .x_0(add_1bit_1_sum));
  My_Multiplexer A1 (.z(A1_z), .y(Add_Sub), .x_1(B[1]), .x_0(add_1bit_2_sum));
  My_Multiplexer A2 (.z(A2_z), .y(Add_Sub), .x_1(B[2]), .x_0(add_1bit_3_sum));
  My_Multiplexer A3 (.z(A3_z), .y(Add_Sub), .x_1(B[3]), .x_0(add_1bit_4_sum));
  Add_1Bit add_1bit_1 (.Cout(add_1bit_1_cout), .Sum(add_1bit_1_sum), .B(not_4_out), .A(not_5_out));  // open: Cin
  Add_1Bit add_1bit_2 (.Cout(add_1bit_2_cout), .Sum(add_1bit_2_sum), .B(not_1_out), .A(Add_Sub), .Cin(add_1bit_1_cout));
  // Probe on A
  Add_1Bit add_1bit_3 (.Cout(add_1bit_3_cout), .Sum(add_1bit_3_sum), .B(not_2_out), .A(Add_Sub), .Cin(add_1bit_2_cout));
  Add_1Bit add_1bit_4 (.Sum(add_1bit_4_sum), .B(not_3_out), .A(Add_Sub), .Cin(add_1bit_3_cout));  // open: Cout
  Add_1Bit add_1bit_5 (.Cout(add_1bit_5_cout), .Sum(R[0]), .B(A[0]), .A(A0_z));  // open: Cin
  Add_1Bit add_1bit_6 (.Cout(add_1bit_6_cout), .Sum(R[1]), .B(A[1]), .A(A1_z), .Cin(add_1bit_5_cout));
  Add_1Bit add_1bit_7 (.Cout(add_1bit_7_cout), .Sum(R[2]), .B(A[2]), .A(A2_z), .Cin(add_1bit_6_cout));
  // Probe on R
  Add_1Bit add_1bit_8 (.Cout(Overflow), .Sum(R[3]), .B(A[3]), .A(A3_z), .Cin(add_1bit_7_cout));
  and and_1 (Zero, ~R[0], ~R[1], ~R[2], ~R[3]);  // AND_Gate

  // Notes on the sheet:
  //   Brandon Smith
  //   MAKE SURE THAT YOU OPEN THIS PROJECT IN "LOGISIM-EVOLUTION"
  //   YOU CAN FIND "LOGISIM-EVOLUTION" PROGRAM IN THE ASSIGNMENT'S FOLDER
  //   DO NOT USE "LOGISIM" VERSION TO SOLVE THIS ASSIGNMENT!
endmodule

module Add_1Bit (
  input  Cin,
  input  A,
  input  B,
  output Cout,
  output Sum
);

  wire and_1_out, and_2_out, xor_1_out;

  and and_1 (and_1_out, A, B);
  xor xor_1 (xor_1_out, A, B);
  or or_1 (Cout, and_1_out, and_2_out);
  and and_2 (and_2_out, Cin, xor_1_out);
  xor xor_2 (Sum, Cin, xor_1_out);

  // Notes on the sheet:
  //   Brandon Smith
  //   MAKE SURE THAT YOU OPENED THIS PROJECT IN "LOGISIM-EVOLUTION"
  //   YOU CAN FIND "LOGISIM-EVOLUTION" PROGRAM IN THE ASSIGNMENT'S FOLDER
  //   DO NOT USE "LOGISIM" VERSION TO SOLVE THIS ASSIGNMENT!
endmodule

module My_Multiplexer (
  input  x_0,
  input  x_1,
  input  y,
  output z
);

  wire and_1_out, and_2_out;

  and and_1 (and_1_out, x_0, ~y);  // AND_Gate
  and and_2 (and_2_out, x_1, y);
  or or_1 (z, and_1_out, and_2_out);
endmodule
