// Logisim project RAM_16_Nibbles_Read_Write.circ as structural Verilog: 3 circuits, main circuit RAM_16_Nibbles
// Clk
module RAM_16_Nibbles (
  input  [3:0] Address,
  input  [3:0] Data,
  input  Read_Write,
  output [3:0] RAM_OUT
);

  wire and_1_out, and_2_out, and_3_out, and_4_out, and_5_out, and_6_out, and_7_out, and_8_out, and_9_out,
       and_10_out, and_11_out, and_12_out, and_13_out, and_14_out, and_15_out, and_16_out, Clk_out, or_1_out,
       or_2_out, or_3_out, or_4_out, or_5_out, or_6_out, or_7_out, or_8_out, or_9_out, or_10_out, or_11_out,
       or_12_out, or_13_out, or_14_out, or_15_out, or_16_out, or_17_out, or_18_out, or_19_out, or_20_out,
       or_21_out, or_22_out, or_23_out, or_24_out, or_25_out, or_26_out, or_27_out, or_28_out, or_31_out,
       or_32_out, or_33_out, or_34_out, or_35_out, or_36_out, or_37_out, or_38_out, or_39_out, or_40_out,
       or_41_out, or_42_out, or_43_out, or_44_out, or_45_out, or_46_out, or_47_out, or_48_out, or_49_out,
       or_50_out, or_51_out, or_52_out, or_53_out, or_54_out, or_55_out, or_56_out, or_57_out, or_58_out;
  wire [3:0] a0000_nibble_out, a0001_nibble_out, a0010_nibble_out, a0011_nibble_out, a0100_nibble_out,
       a0101_nibble_out, a0110_nibble_out, a0111_nibble_out, a1000_nibble_out, a1001_nibble_out,
       a1010_nibble_out, a1011_nibble_out, a1100_nibble_out, a1101_nibble_out, a1110_nibble_out,
       a1111_nibble_out;

  // Probe on Address
  Clock Clk (.out(Clk_out));
  and and_1 (and_1_out, ~Address[3], ~Address[2], ~Address[1], ~Address[0]);  // AND_Gate
  and and_2 (and_2_out, ~Address[3], ~Address[2], ~Address[1], Address[0]);  // AND_Gate
  and and_3 (and_3_out, ~Address[3], ~Address[2], Address[1], ~Address[0]);  // AND_Gate
  and and_4 (and_4_out, ~Address[3], ~Address[2], Address[1], Address[0]);  // AND_Gate
  and and_5 (and_5_out, ~Address[3], Address[2], ~Address[1], ~Address[0]);  // AND_Gate
  and and_6 (and_6_out, ~Address[3], Address[2], ~Address[1], Address[0]);  // AND_Gate
  and and_7 (and_7_out, ~Address[3], Address[2], Address[1], ~Address[0]);  // AND_Gate
  and and_8 (and_8_out, ~Address[3], Address[2], Address[1], Address[0]);  // AND_Gate
  and and_9 (and_9_out, Address[3], ~Address[2], ~Address[1], ~Address[0]);  // AND_Gate
  and and_10 (and_10_out, Address[3], ~Address[2], ~Address[1], Address[0]);  // AND_Gate
  and and_11 (and_11_out, Address[3], ~Address[2], Address[1], ~Address[0]);  // AND_Gate
  and and_12 (and_12_out, Address[3], ~Address[2], Address[1], Address[0]);  // AND_Gate
  and and_13 (and_13_out, Address[3], Address[2], ~Address[1], ~Address[0]);  // AND_Gate
  and and_14 (and_14_out, Address[3], Address[2], ~Address[1], Address[0]);  // AND_Gate
  and and_15 (and_15_out, Address[3], Address[2], Address[1], ~Address[0]);  // AND_Gate
  and and_16 (and_16_out, Address[3], Address[2], Address[1], Address[0]);
  // Probe on Data
  Nibble a0000 (.Nibble_Out(a0000_nibble_out), .Read_Write(Read_Write), .Enable(and_1_out), .Clk(Clk_out), .Data(Data));
  Nibble a0001 (.Nibble_Out(a0001_nibble_out), .Read_Write(Read_Write), .Enable(and_2_out), .Clk(Clk_out), .Data(Data));
  or or_1 (or_1_out, a0001_nibble_out[3], a0000_nibble_out[3]);
  or or_2 (or_2_out, a0001_nibble_out[2], a0000_nibble_out[2]);
  Nibble a0010 (.Nibble_Out(a0010_nibble_out), .Read_Write(Read_Write), .Enable(and_3_out), .Clk(Clk_out), .Data(Data));
  or or_3 (or_3_out, a0010_nibble_out[3], or_1_out);
  or or_4 (or_4_out, a0010_nibble_out[2], or_2_out);
  Nibble a0011 (.Nibble_Out(a0011_nibble_out), .Read_Write(Read_Write), .Enable(and_4_out), .Clk(Clk_out), .Data(Data));
  or or_5 (or_5_out, a0011_nibble_out[3], or_3_out);
  or or_6 (or_6_out, a0011_nibble_out[2], or_4_out);
  Nibble a0100 (.Nibble_Out(a0100_nibble_out), .Read_Write(Read_Write), .Enable(and_5_out), .Clk(Clk_out), .Data(Data));
  or or_7 (or_7_out, a0100_nibble_out[2], or_6_out);
  or or_8 (or_8_out, a0100_nibble_out[3], or_5_out);
  Nibble a0101 (.Nibble_Out(a0101_nibble_out), .Read_Write(Read_Write), .Enable(and_6_out), .Clk(Clk_out), .Data(Data));
  or or_9 (or_9_out, a0101_nibble_out[3], or_8_out);
  or or_10 (or_10_out, a0101_nibble_out[2], or_7_out);
  Nibble a0110 (.Nibble_Out(a0110_nibble_out), .Read_Write(Read_Write), .Enable(and_7_out), .Clk(Clk_out), .Data(Data));
  or or_11 (or_11_out, a0110_nibble_out[3], or_9_out);
  or or_12 (or_12_out, a0110_nibble_out[2], or_10_out);
  Nibble a0111 (.Nibble_Out(a0111_nibble_out), .Read_Write(Read_Write), .Enable(and_8_out), .Clk(Clk_out), .Data(Data));
  or or_13 (or_13_out, a0111_nibble_out[3], or_11_out);
  or or_14 (or_14_out, a0111_nibble_out[2], or_12_out);
  Nibble a1000 (.Nibble_Out(a1000_nibble_out), .Read_Write(Read_Write), .Enable(and_9_out), .Clk(Clk_out), .Data(Data));
  or or_15 (or_15_out, a1000_nibble_out[2], or_14_out);
  or or_16 (or_16_out, a1000_nibble_out[3], or_13_out);
  Nibble a1001 (
    .Nibble_Out(a1001_nibble_out), .Read_Write(Read_Write), .Enable(and_10_out), .Clk(Clk_out), .Data(Data));
  or or_17 (or_17_out, a1001_nibble_out[2], or_15_out);
  or or_18 (or_18_out, a1001_nibble_out[3], or_16_out);
  Nibble a1010 (
    .Nibble_Out(a1010_nibble_out), .Read_Write(Read_Write), .Enable(and_11_out), .Clk(Clk_out), .Data(Data));
  or or_19 (or_19_out, a1010_nibble_out[3], or_18_out);
  or or_20 (or_20_out, a1010_nibble_out[2], or_17_out);
  Nibble a1011 (
    .Nibble_Out(a1011_nibble_out), .Read_Write(Read_Write), .Enable(and_12_out), .Clk(Clk_out), .Data(Data));
  or or_21 (or_21_out, a1011_nibble_out[3], or_19_out);
  or or_22 (or_22_out, a1011_nibble_out[2], or_20_out);
  Nibble a1100 (
    .Nibble_Out(a1100_nibble_out), .Read_Write(Read_Write), .Enable(and_13_out), .Clk(Clk_out), .Data(Data));
  or or_23 (or_23_out, a1100_nibble_out[2], or_22_out);
  or or_24 (or_24_out, a1100_nibble_out[3], or_21_out);
  Nibble a1101 (
    .Nibble_Out(a1101_nibble_out), .Read_Write(Read_Write), .Enable(and_14_out), .Clk(Clk_out), .Data(Data));
  or or_25 (or_25_out, a1101_nibble_out[3], or_24_out);
  or or_26 (or_26_out, a1101_nibble_out[2], or_23_out);
  Nibble a1110 (
    .Nibble_Out(a1110_nibble_out), .Read_Write(Read_Write), .Enable(and_15_out), .Clk(Clk_out), .Data(Data));
  or or_27 (or_27_out, a1110_nibble_out[3], or_25_out);
  or or_28 (or_28_out, a1110_nibble_out[2], or_26_out);
  Nibble a1111 (
    .Nibble_Out(a1111_nibble_out), .Read_Write(Read_Write), .Enable(and_16_out), .Clk(Clk_out), .Data(Data));
  or or_29 (RAM_OUT[3], a1111_nibble_out[3], or_27_out);
  or or_30 (RAM_OUT[2], a1111_nibble_out[2], or_28_out);
  or or_31 (or_31_out, a0001_nibble_out[1], a0000_nibble_out[1]);
  or or_32 (or_32_out, a0001_nibble_out[0], a0000_nibble_out[0]);
  or or_33 (or_33_out, a0010_nibble_out[0], or_32_out);
  or or_34 (or_34_out, a0010_nibble_out[1], or_31_out);
  or or_35 (or_35_out, a0011_nibble_out[0], or_33_out);
  or or_36 (or_36_out, a0011_nibble_out[1], or_34_out);
  or or_37 (or_37_out, a0100_nibble_out[0], or_35_out);
  or or_38 (or_38_out, a0100_nibble_out[1], or_36_out);
  or or_39 (or_39_out, a0101_nibble_out[0], or_37_out);
  or or_40 (or_40_out, a0101_nibble_out[1], or_38_out);
  or or_41 (or_41_out, a0110_nibble_out[1], or_40_out);
  or or_42 (or_42_out, a0110_nibble_out[0], or_39_out);
  or or_43 (or_43_out, a0111_nibble_out[1], or_41_out);
  or or_44 (or_44_out, a0111_nibble_out[0], or_42_out);
  or or_45 (or_45_out, a1000_nibble_out[0], or_44_out);
  or or_46 (or_46_out, a1000_nibble_out[1], or_43_out);
  or or_47 (or_47_out, a1001_nibble_out[1], or_46_out);
  or or_48 (or_48_out, a1001_nibble_out[0], or_45_out);
  or or_49 (or_49_out, a1010_nibble_out[1], or_47_out);
  or or_50 (or_50_out, a1010_nibble_out[0], or_48_out);
  or or_51 (or_51_out, a1011_nibble_out[1], or_49_out);
  or or_52 (or_52_out, a1011_nibble_out[0], or_50_out);
  or or_53 (or_53_out, a1100_nibble_out[1], or_51_out);
  or or_54 (or_54_out, a1100_nibble_out[0], or_52_out);
  or or_55 (or_55_out, a1101_nibble_out[1], or_53_out);
  or or_56 (or_56_out, a1101_nibble_out[0], or_54_out);
  or or_57 (or_57_out, a1110_nibble_out[1], or_55_out);
  or or_58 (or_58_out, a1110_nibble_out[0], or_56_out);
  or or_59 (RAM_OUT[1], a1111_nibble_out[1], or_57_out);
  or or_60 (RAM_OUT[0], a1111_nibble_out[0], or_58_out);
  // Probe on RAM_OUT

  // Notes on the sheet:
  //   Brandon Smith
  //   Dear TA,
  //   My RAM is implemented with the
  //   enable line managing both read
  //   and write operations so that the
  //   addressing need not be duplicated
  //   on the right of my 16 nibbles.
  //   When Read_Write = 1 performs read, otherwise performs write
  //   MAKE SURE THAT YOU OPEN THIS PROJECT IN "LOGISIM-EVOLUTION"
  //   YOU CAN FIND "LOGISIM-EVOLUTION" PROGRAM IN THE ASSIGNMENT'S FOLDER
  //   DO NOT USE "LOGISIM" VERSION TO SOLVE THIS ASSIGNMENT!
endmodule

module Nibble (
  input  Enable,
  input  Clk,
  input  Read_Write,
  input  [3:0] Data,
  output [3:0] Nibble_Out
);

  wire and_1_out, and_2_out, and_3_out, and_4_out, and_5_out, and_6_out, and_7_out, and_8_out, and_9_out,
       and_14_out, not_1_out, not_2_out, not_3_out, not_4_out, not_5_out, rsflipflop_1_q, rsflipflop_2_q,
       rsflipflop_3_q, rsflipflop_4_q;

  not not_1 (not_1_out, Data[0]);
  not not_2 (not_2_out, Data[1]);
  not not_3 (not_3_out, Data[2]);
  not not_4 (not_4_out, Data[3]);
  and and_1 (and_1_out, not_5_out, Clk, Enable);
  // Probe on Data
  and and_2 (and_2_out, not_1_out, and_1_out);
  and and_3 (and_3_out, Data[0], and_1_out);
  and and_4 (and_4_out, not_2_out, and_1_out);
  and and_5 (and_5_out, Data[1], and_1_out);
  and and_6 (and_6_out, not_3_out, and_1_out);
  and and_7 (and_7_out, Data[2], and_1_out);
  and and_8 (and_8_out, not_4_out, and_1_out);
  and and_9 (and_9_out, Data[3], and_1_out);
  not not_5 (not_5_out, Read_Write);
  RSFlipFlop rsflipflop_1 (.Q(rsflipflop_1_q), .S(and_3_out), .R(and_2_out));
  and and_10 (Nibble_Out[0], rsflipflop_1_q, and_14_out);
  RSFlipFlop rsflipflop_2 (.Q(rsflipflop_2_q), .S(and_5_out), .R(and_4_out));
  and and_11 (Nibble_Out[1], rsflipflop_2_q, and_14_out);
  RSFlipFlop rsflipflop_3 (.Q(rsflipflop_3_q), .S(and_7_out), .R(and_6_out));
  and and_12 (Nibble_Out[2], rsflipflop_3_q, and_14_out);
  RSFlipFlop rsflipflop_4 (.Q(rsflipflop_4_q), .S(and_9_out), .R(and_8_out));
  and and_13 (Nibble_Out[3], rsflipflop_4_q, and_14_out);
  and and_14 (and_14_out, Enable, Clk, Read_Write);
  // Probe on Nibble_Out

  // Notes on the sheet:
  //   Brandon Smith
  //   When Read_Write = 1 performs read, otherwise performs write
  //   MAKE SURE THAT YOU OPEN THIS PROJECT IN "LOGISIM-EVOLUTION"
  //   YOU CAN FIND "LOGISIM-EVOLUTION" PROGRAM IN THE ASSIGNMENT'S FOLDER
  //   DO NOT USE "LOGISIM" VERSION TO SOLVE THIS ASSIGNMENT!
endmodule

module RSFlipFlop (
  input  R,
  input  S,
  output Q
);

  wire not_2_out, or_1_out, or_2_out;

  or or_1 (or_1_out, R, not_2_out);
  not not_1 (Q, or_1_out);
  not not_2 (not_2_out, or_2_out);
  or or_2 (or_2_out, Q, S);
endmodule
