// Logisim project Question3.circ as structural Verilog: 7 circuits, main circuit main
module main (
  input  [7:0] IR_In,
  input  in_2,
  input  in_3
);

  wire clock_1_out, controlunit_1_comparitor_addressing, controlunit_1_r1_addressing,
       controlunit_1_r1_readwrite, controlunit_1_r2_addressing, controlunit_1_r2_readwrite,
       mycomparitor_1_equality, or_1_out, or_2_out, or_5_out, or_6_out;
  wire [3:0] controlunit_1_data_out, or_7_out, R1_data_out, R2_data_out;
  wire [7:0] myregister_8bit_1_data_out;

  Clock clock_1 (.out(clock_1_out));
  myRegister_8bit myregister_8bit_1 (
    .Data_In(IR_In), .CLK(clock_1_out), .ReadWrite(in_2), .Addressing(in_3),
    .Data_Out(myregister_8bit_1_data_out));
  ControlUnit controlunit_1 (
    .IR_In(myregister_8bit_1_data_out), .Comparitor_Result(mycomparitor_1_equality),
    .R1_Addressing(controlunit_1_r1_addressing), .R2_Addressing(controlunit_1_r2_addressing),
    .R1_ReadWrite(controlunit_1_r1_readwrite), .R2_ReadWrite(controlunit_1_r2_readwrite),
    .Comparitor_Addressing(controlunit_1_comparitor_addressing), .Data_Out(controlunit_1_data_out));
  myRegister_Nibble R1 (
    .Data_In(or_7_out), .CLK(clock_1_out), .Addressing(controlunit_1_r1_addressing),
    .ReadWrite(controlunit_1_r1_readwrite), .Data_Out(R1_data_out));
  myRegister_Nibble R2 (
    .Data_In(or_7_out), .CLK(clock_1_out), .Addressing(controlunit_1_r2_addressing),
    .ReadWrite(controlunit_1_r2_readwrite), .Data_Out(R2_data_out));
  myComparitor mycomparitor_1 (
    .In_0(or_7_out), .In_1(controlunit_1_data_out), .Addressing(controlunit_1_comparitor_addressing),
    .Equality(mycomparitor_1_equality));
  or or_1 (or_1_out, R1_data_out[3], controlunit_1_data_out[3]);
  or or_2 (or_2_out, R1_data_out[2], controlunit_1_data_out[2]);
  or or_3 (or_7_out[2], R2_data_out[2], or_2_out);
  or or_4 (or_7_out[3], R2_data_out[3], or_1_out);
  or or_5 (or_5_out, R1_data_out[1], controlunit_1_data_out[1]);
  or or_6 (or_6_out, R1_data_out[0], controlunit_1_data_out[0]);
  or or_7 (or_7_out[0], R2_data_out[0], or_6_out);
  or or_8 (or_7_out[1], R2_data_out[1], or_5_out);

  // Notes on the sheet:
  //   Brandon Smith
  //   Read = 0, Write = 1
  //   Assumed that R1 has address 000
  //   Assumed that R2 has address 001
  //   Sorry to make you have to look over this abomination of a circuit (it doesn't even function).  Life decided I wasn't gonna have enough time for this assignment :(
endmodule

module myFlipFlop (
  input  R,
  input  S,
  output Q
);

  wire not_2_out, or_1_out, or_2_out;

  or or_1 (or_1_out, R, not_2_out);
  or or_2 (or_2_out, Q, S);
  not not_1 (Q, or_1_out);
  not not_2 (not_2_out, or_2_out);

  // Notes on the sheet:
  //   Brandon Smith
endmodule

module myRegister_8bit (
  input  [7:0] Data_In,
  input  CLK,
  input  ReadWrite,
  input  Addressing,
  output [7:0] Data_Out
);

  wire and_1_out, and_2_out, and_3_out, and_4_out, and_5_out, and_6_out, and_7_out, and_8_out, and_9_out,
       and_10_out, and_11_out, and_12_out, and_13_out, and_14_out, and_15_out, and_16_out, and_17_out,
       and_26_out, myflipflop_1_q, myflipflop_2_q, myflipflop_3_q, myflipflop_4_q, myflipflop_5_q,
       myflipflop_6_q, myflipflop_7_q, myflipflop_8_q, not_1_out, not_2_out, not_3_out, not_4_out, not_5_out,
       not_6_out, not_7_out, not_8_out, not_9_out;

  not not_1 (not_1_out, Data_In[0]);
  and and_1 (and_1_out, not_1_out, and_17_out);
  and and_2 (and_2_out, Data_In[0], and_17_out);
  not not_2 (not_2_out, Data_In[1]);
  and and_3 (and_3_out, not_2_out, and_17_out);
  and and_4 (and_4_out, Data_In[1], and_17_out);
  not not_3 (not_3_out, Data_In[2]);
  and and_5 (and_5_out, not_3_out, and_17_out);
  and and_6 (and_6_out, Data_In[2], and_17_out);
  not not_4 (not_4_out, Data_In[3]);
  and and_7 (and_7_out, not_4_out, and_17_out);
  and and_8 (and_8_out, Data_In[3], and_17_out);
  not not_5 (not_5_out, Data_In[4]);
  and and_9 (and_9_out, not_5_out, and_17_out);
  and and_10 (and_10_out, Data_In[4], and_17_out);
  not not_6 (not_6_out, Data_In[5]);
  and and_11 (and_11_out, not_6_out, and_17_out);
  and and_12 (and_12_out, Data_In[5], and_17_out);
  not not_7 (not_7_out, Data_In[6]);
  and and_13 (and_13_out, not_7_out, and_17_out);
  and and_14 (and_14_out, Data_In[6], and_17_out);
  not not_8 (not_8_out, Data_In[7]);
  and and_15 (and_15_out, not_8_out, and_17_out);
  and and_16 (and_16_out, Data_In[7], and_17_out);
  and and_17 (and_17_out, CLK, ReadWrite);
  myFlipFlop myflipflop_1 (.Q(myflipflop_1_q), .S(and_2_out), .R(and_1_out));
  myFlipFlop myflipflop_2 (.Q(myflipflop_2_q), .S(and_4_out), .R(and_3_out));
  myFlipFlop myflipflop_3 (.Q(myflipflop_3_q), .S(and_6_out), .R(and_5_out));
  myFlipFlop myflipflop_4 (.Q(myflipflop_4_q), .S(and_8_out), .R(and_7_out));
  myFlipFlop myflipflop_5 (.Q(myflipflop_5_q), .S(and_10_out), .R(and_9_out));
  myFlipFlop myflipflop_6 (.Q(myflipflop_6_q), .S(and_12_out), .R(and_11_out));
  myFlipFlop myflipflop_7 (.Q(myflipflop_7_q), .S(and_14_out), .R(and_13_out));
  myFlipFlop myflipflop_8 (.Q(myflipflop_8_q), .S(and_16_out), .R(and_15_out));
  not not_9 (not_9_out, ReadWrite);
  and and_18 (Data_Out[0], myflipflop_1_q, and_26_out);
  and and_19 (Data_Out[1], myflipflop_2_q, and_26_out);
  and and_20 (Data_Out[2], myflipflop_3_q, and_26_out);
  and and_21 (Data_Out[3], myflipflop_4_q, and_26_out);
  and and_22 (Data_Out[4], myflipflop_5_q, and_26_out);
  and and_23 (Data_Out[5], myflipflop_6_q, and_26_out);
  and and_24 (Data_Out[6], myflipflop_7_q, and_26_out);
  and and_25 (Data_Out[7], myflipflop_8_q, and_26_out);
  and and_26 (and_26_out, not_9_out, CLK);

  // Notes on the sheet:
  //   Brandon Smith
endmodule

module myRegister_Nibble (
  input  [3:0] Data_In,
  input  CLK,
  input  Addressing,
  input  ReadWrite,
  output [3:0] Data_Out
);

  wire and_1_out, and_2_out, and_3_out, and_4_out, and_5_out, and_6_out, and_7_out, and_8_out, and_9_out,
       and_14_out, myflipflop_1_q, myflipflop_2_q, myflipflop_3_q, myflipflop_4_q, not_1_out, not_2_out,
       not_3_out, not_4_out, not_5_out;

  // Probe on Data_In
  not not_1 (not_1_out, Data_In[0]);
  and and_1 (and_1_out, not_1_out, and_9_out);
  and and_2 (and_2_out, Data_In[0], and_9_out);
  not not_2 (not_2_out, Data_In[1]);
  and and_3 (and_3_out, not_2_out, and_9_out);
  and and_4 (and_4_out, Data_In[1], and_9_out);
  not not_3 (not_3_out, Data_In[2]);
  and and_5 (and_5_out, not_3_out, and_9_out);
  and and_6 (and_6_out, Data_In[2], and_9_out);
  not not_4 (not_4_out, Data_In[3]);
  and and_7 (and_7_out, not_4_out, and_9_out);
  and and_8 (and_8_out, Data_In[3], and_9_out);
  and and_9 (and_9_out, Addressing, CLK, ReadWrite);
  myFlipFlop myflipflop_1 (.Q(myflipflop_1_q), .S(and_2_out), .R(and_1_out));
  myFlipFlop myflipflop_2 (.Q(myflipflop_2_q), .S(and_4_out), .R(and_3_out));
  myFlipFlop myflipflop_3 (.Q(myflipflop_3_q), .S(and_6_out), .R(and_5_out));
  myFlipFlop myflipflop_4 (.Q(myflipflop_4_q), .S(and_8_out), .R(and_7_out));
  not not_5 (not_5_out, ReadWrite);
  and and_10 (Data_Out[0], myflipflop_1_q, and_14_out);
  and and_11 (Data_Out[1], myflipflop_2_q, and_14_out);
  and and_12 (Data_Out[2], myflipflop_3_q, and_14_out);
  and and_13 (Data_Out[3], myflipflop_4_q, and_14_out);
  and and_14 (and_14_out, not_5_out, CLK, Addressing);
  // Probe on Data_Out

  // Notes on the sheet:
  //   Brandon Smith
endmodule

module ControlUnit (
  input  [7:0] IR_In,
  input  Comparitor_Result,
  output R1_Addressing,
  output R2_Addressing,
  output R1_ReadWrite,
  output R2_ReadWrite,
  output Comparitor_Addressing,
  output [3:0] Data_Out
);

  wire and_1_out, and_2_out, and_3_out, and_4_out, and_5_out, and_6_out;

  and and_1 (and_1_out, IR_In[7], IR_In[6]);
  and and_2 (and_2_out, ~IR_In[7], ~IR_In[6]);  // AND_Gate
  and and_3 (and_3_out, ~IR_In[5], ~IR_In[4], ~IR_In[3], and_2_out);  // AND_Gate
  and and_4 (and_4_out, ~IR_In[2], ~IR_In[1], IR_In[0], and_2_out);  // AND_Gate
  and and_5 (and_5_out, ~IR_In[2], ~IR_In[1], ~IR_In[0], and_2_out);  // AND_Gate
  and and_6 (and_6_out, ~IR_In[5], ~IR_In[4], IR_In[3], and_2_out);  // AND_Gate
  or or_1 (R1_Addressing, and_3_out, and_5_out);
  or or_2 (R2_Addressing, and_4_out, and_6_out);
  buf or_3 (R1_ReadWrite, and_5_out);  // OR_Gate
  buf or_4 (R2_ReadWrite, and_4_out);  // OR_Gate
  // OR_Gate or_5 has open pins: out=Comparitor_Addressing

  // Notes on the sheet:
  //   Brandon Smith
endmodule

module My_Multiplexer (
  input  x_0,
  input  x_1,
  input  y,
  output z
);

  wire and_1_out, and_2_out;

  and and_1 (and_1_out, x_0, ~y);  // AND_Gate
  and and_2 (and_2_out, x_1, y);
  or or_1 (z, and_1_out, and_2_out);

  // Notes on the sheet:
  //   Brandon Smith
endmodule

module myComparitor (
  input  [3:0] In_0,
  input  [3:0] In_1,
  input  Addressing,
  output Equality
);

  wire and_1_out, not_1_out, not_2_out, not_3_out, not_4_out, xor_1_out, xor_2_out, xor_3_out, xor_4_out;

  not not_1 (not_1_out, xor_1_out);
  xor xor_1 (xor_1_out, In_0[0], In_1[0]);
  xor xor_2 (xor_2_out, In_0[1], In_1[1]);
  not not_2 (not_2_out, xor_2_out);
  xor xor_3 (xor_3_out, In_0[2], In_1[2]);
  not not_3 (not_3_out, xor_3_out);
  not not_4 (not_4_out, xor_4_out);
  xor xor_4 (xor_4_out, In_0[3], In_1[3]);
  and and_1 (and_1_out, not_1_out, not_2_out, not_3_out, not_4_out);
  and and_2 (Equality, and_1_out, Addressing);

  // Notes on the sheet:
  //   Brandon Smith
endmodule
