// Logisim project Multi_Instruction_CPU.circ as structural Verilog: 12 circuits, main circuit main
module main (
  input  Register_Set,
  input  [3:0] RAM_Set,
  input  [1:0] RAM_Addressing,
  input  RAM_Override,
  input  [1:0] PC_Set,
  input  PC_Override,
  output [1:0] out_7
);

  wire and_1_out, clock_1_out, fetchcontrolunit_1_instrcu_addressing, fetchcontrolunit_1_ir_addressing,
       fetchcontrolunit_1_ir_readwrite, fetchcontrolunit_1_microstepout, fetchcontrolunit_1_pc_increment,
       instructioncontrolunit_1_aout_addressing, instructioncontrolunit_1_aout_readwrite,
       instructioncontrolunit_1_lr_addressing, instructioncontrolunit_1_lr_readwrite,
       instructioncontrolunit_1_ram_readwrite, instructioncontrolunit_1_status_readwrite,
       instructioncontrolunit_1_stop_out, not_1_out, not_2_out, not_3_out, not_4_out, not_5_out, not_6_out,
       not_7_out, or_1_out, or_4_out, or_5_out, rsflipflop_1_q;
  wire [1:0] alu_1_status, and_3_out, and_8_out, incrementer_1_inc_out, my_multiplexer_1_z,
       my_multiplexer_3_z, or_3_out, PC_data_out, register_2bit_1_data_out;
  wire [3:0] A_Out_data_out, alu_1_sum, and_4_out, IR_data_out, L_data_out, or_2_out, R_data_out, RAM_ram_out;

  Clock clock_1 (.out(clock_1_out));
  and and_1 (and_1_out, fetchcontrolunit_1_pc_increment, ~rsflipflop_1_q);  // AND_Gate
  not not_1 (not_1_out, and_1_out);
  or or_1 (or_1_out, and_1_out, PC_Override);
  assign or_2_out = and_4_out | RAM_Set;  // OR_Gate or_2, 4 bits wide
  and and_2 (and_3_out[1], not_7_out, PC_data_out[1]);
  and and_3 (and_3_out[0], not_7_out, PC_data_out[0]);
  not not_2 (not_2_out, not_4_out);
  RSFlipFlop rsflipflop_1 (.R(PC_Override), .S(instructioncontrolunit_1_stop_out), .Q(rsflipflop_1_q));
  My_Multiplexer my_multiplexer_1 (
    .x_0(register_2bit_1_data_out[0]), .x_1(PC_Set[0]), .y(PC_Override), .z(my_multiplexer_1_z[0]));
  My_Multiplexer my_multiplexer_2 (
    .x_0(register_2bit_1_data_out[1]), .x_1(PC_Set[1]), .y(PC_Override), .z(my_multiplexer_1_z[1]));
  and and_4 (and_4_out[0], A_Out_data_out[0], not_3_out);
  and and_5 (and_4_out[1], A_Out_data_out[1], not_3_out);
  and and_6 (and_4_out[2], A_Out_data_out[2], not_3_out);
  and and_7 (and_4_out[3], A_Out_data_out[3], not_3_out);
  not not_3 (not_3_out, RAM_Override);
  assign or_3_out = RAM_Addressing | and_8_out | and_3_out;  // OR_Gate or_3, 2 bits wide
  not not_4 (not_4_out, not_5_out);
  not not_5 (not_5_out, not_6_out);
  not not_6 (not_6_out, instructioncontrolunit_1_ram_readwrite);
  or or_4 (or_4_out, not_2_out, RAM_Override);
  or or_5 (or_5_out, clock_1_out, RAM_Override);
  Register_2bit PC (
    .Data_In(my_multiplexer_1_z), .CLK(1'b1), .Addressing(1'b1), .ReadWrite(not_1_out), .Data_Out(PC_data_out));
  Register_2bit register_2bit_1 (
    .Data_In(my_multiplexer_3_z), .CLK(1'b1), .Addressing(1'b1), .ReadWrite(or_1_out),
    .Data_Out(register_2bit_1_data_out));
  My_Multiplexer my_multiplexer_3 (
    .x_0(incrementer_1_inc_out[0]), .x_1(PC_Set[0]), .y(PC_Override), .z(my_multiplexer_3_z[0]));
  My_Multiplexer my_multiplexer_4 (
    .x_0(incrementer_1_inc_out[1]), .x_1(PC_Set[1]), .y(PC_Override), .z(my_multiplexer_3_z[1]));
  RAM_4_Nibble RAM (.Data(or_2_out), .ReadWrite(or_4_out), .CLK(or_5_out), .Address(or_3_out), .RAM_Out(RAM_ram_out));
  Incrementer incrementer_1 (.Inc_In(PC_data_out), .Inc_Out(incrementer_1_inc_out));
  and and_8 (and_8_out[0], IR_data_out[0], instructioncontrolunit_1_ram_readwrite);
  and and_9 (and_8_out[1], IR_data_out[1], instructioncontrolunit_1_ram_readwrite);
  not not_7 (not_7_out, instructioncontrolunit_1_ram_readwrite);
  FetchControlUnit fetchcontrolunit_1 (
    .CLK(clock_1_out), .Fectch_Set(PC_Set), .FetchCU_Override(PC_Override),
    .IR_Addressing(fetchcontrolunit_1_ir_addressing), .IR_ReadWrite(fetchcontrolunit_1_ir_readwrite),
    .InstrCU_Addressing(fetchcontrolunit_1_instrcu_addressing),
    .MicroStepOut(fetchcontrolunit_1_microstepout), .PC_Increment(fetchcontrolunit_1_pc_increment));
  Register_Nibble IR (
    .Data_In(RAM_ram_out), .Register_Reset(Register_Set), .CLK(clock_1_out),
    .Addressing(fetchcontrolunit_1_ir_addressing), .ReadWrite(fetchcontrolunit_1_ir_readwrite),
    .Data_Out(IR_data_out));
  InstructionControlUnit instructioncontrolunit_1 (
    .IR_In(IR_data_out), .MicroStep(fetchcontrolunit_1_microstepout),
    .Addressing(fetchcontrolunit_1_instrcu_addressing),
    .LR_Addressing(instructioncontrolunit_1_lr_addressing),
    .LR_ReadWrite(instructioncontrolunit_1_lr_readwrite),
    .Aout_Addressing(instructioncontrolunit_1_aout_addressing),
    .Aout_ReadWrite(instructioncontrolunit_1_aout_readwrite),
    .Status_ReadWrite(instructioncontrolunit_1_status_readwrite),
    .RAM_ReadWrite(instructioncontrolunit_1_ram_readwrite), .STOP_Out(instructioncontrolunit_1_stop_out));
  Register_Nibble L (
    .Data_In(IR_data_out), .Register_Reset(Register_Set), .CLK(clock_1_out),
    .Addressing(instructioncontrolunit_1_lr_addressing), .ReadWrite(instructioncontrolunit_1_lr_readwrite),
    .Data_Out(L_data_out));
  Register_Nibble R (
    .Data_In(IR_data_out), .Register_Reset(Register_Set), .CLK(clock_1_out),
    .Addressing(instructioncontrolunit_1_lr_addressing), .ReadWrite(instructioncontrolunit_1_lr_readwrite),
    .Data_Out(R_data_out));
  ALU alu_1 (.A(L_data_out), .B(R_data_out), .Sum(alu_1_sum), .Status(alu_1_status));
  Register_2bit Status (
    .Data_In(alu_1_status), .CLK(1'b1), .Addressing(1'b1),
    .ReadWrite(instructioncontrolunit_1_status_readwrite), .Data_Out(out_7));
  Register_Nibble A_Out (
    .Data_In(alu_1_sum), .Register_Reset(Register_Set), .CLK(clock_1_out),
    .Addressing(instructioncontrolunit_1_aout_addressing),
    .ReadWrite(instructioncontrolunit_1_aout_readwrite), .Data_Out(A_Out_data_out));

  // Notes on the sheet:
  //   Brandon Smith
  //   INSTRUCTIONS FOR EXECUTION:
  //   1) Scroll down to the bottom left of the circuit, and set PC_Override to 1
  //   2) Set PC_Override back to 0
  //   3) Scroll back up to the top left of the circuit, and set Register_Set to 1
  //   4) Set Register_Set back to 0
  //   5) Set RAM_Set to desired instruction
  //   6) Set RAM_Addressing to desired RAM address
  //   7) Set RAM_Override to 1
  //   8) Set RAM_Override back to 0
  //   9) Return to step 5 until RAM is initialized as desired
  //   10) Ensure that RAM_SET, RAM_Addressing, and RAM_Override are ALL 0
  //   11) Begin CLK ticks
endmodule

module Add_1Bit (
  input  Cin,
  input  A,
  input  B,
  output Cout,
  output Sum
);

  wire and_1_out, and_2_out, xor_1_out;

  and and_1 (and_1_out, A, B);
  xor xor_1 (xor_1_out, A, B);
  or or_1 (Cout, and_1_out, and_2_out);
  and and_2 (and_2_out, Cin, xor_1_out);
  xor xor_2 (Sum, Cin, xor_1_out);

  // Notes on the sheet:
  //   Brandon Smith
endmodule

module My_Multiplexer (
  input  x_0,
  input  x_1,
  input  y,
  output z
);

  wire and_1_out, and_2_out;

  and and_1 (and_1_out, x_0, ~y);  // AND_Gate
  and and_2 (and_2_out, x_1, y);
  or or_1 (z, and_1_out, and_2_out);

  // Notes on the sheet:
  //   Brandon Smith
endmodule

module ALU (
  input  [3:0] A,
  input  [3:0] B,
  output [3:0] Sum,
  output [1:0] Status
);

  wire add_1bit_1_cout, add_1bit_2_cout, add_1bit_3_cout, not_1_out;

  // Probe on A
  // Probe on B
  Add_1Bit add_1bit_1 (.A(A[0]), .B(B[0]), .Cout(add_1bit_1_cout), .Sum(Sum[0]));  // open: Cin
  Add_1Bit add_1bit_2 (.Cin(add_1bit_1_cout), .A(A[1]), .B(B[1]), .Cout(add_1bit_2_cout), .Sum(Sum[1]));
  Add_1Bit add_1bit_3 (.Cin(add_1bit_2_cout), .A(A[2]), .B(B[2]), .Cout(add_1bit_3_cout), .Sum(Sum[2]));
  not not_1 (not_1_out, 1'b1);
  // Probe on Sum
  Add_1Bit add_1bit_4 (.Cin(add_1bit_3_cout), .A(not_1_out), .B(not_1_out), .Cout(Status[1]), .Sum(Sum[3]));
  and and_1 (Status[0], ~Sum[0], ~Sum[1], ~Sum[2], ~Sum[3]);  // AND_Gate

  // Notes on the sheet:
  //   Brandon Smith
endmodule

module RSFlipFlop (
  input  R,
  input  S,
  output Q
);

  wire not_2_out, or_1_out, or_2_out;

  or or_1 (or_1_out, R, not_2_out);
  not not_1 (Q, or_1_out);
  or or_2 (or_2_out, Q, S);
  not not_2 (not_2_out, or_2_out);

  // Notes on the sheet:
  //   Brandon Smith
endmodule

module Nibble (
  input  Enable,
  input  CLK,
  input  ReadWrite,
  input  [3:0] Data,
  output [3:0] NibbleOut
);

  wire and_1_out, and_2_out, and_3_out, and_4_out, and_5_out, and_6_out, and_7_out, and_8_out, and_9_out,
       not_1_out, not_2_out, not_3_out, not_4_out, rsflipflop_1_q, rsflipflop_2_q, rsflipflop_3_q,
       rsflipflop_4_q;

  not not_1 (not_1_out, Data[0]);
  not not_2 (not_2_out, Data[1]);
  not not_3 (not_3_out, Data[2]);
  not not_4 (not_4_out, Data[3]);
  and and_1 (and_1_out, ReadWrite, CLK, Enable);
  // Probe on Data
  and and_2 (and_2_out, not_1_out, and_1_out);
  and and_3 (and_3_out, Data[0], and_1_out);
  and and_4 (and_4_out, not_2_out, and_1_out);
  and and_5 (and_5_out, Data[1], and_1_out);
  and and_6 (and_6_out, not_3_out, and_1_out);
  and and_7 (and_7_out, Data[2], and_1_out);
  and and_8 (and_8_out, not_4_out, and_1_out);
  and and_9 (and_9_out, Data[3], and_1_out);
  RSFlipFlop rsflipflop_1 (.R(and_2_out), .S(and_3_out), .Q(rsflipflop_1_q));
  RSFlipFlop rsflipflop_2 (.R(and_4_out), .S(and_5_out), .Q(rsflipflop_2_q));
  RSFlipFlop rsflipflop_3 (.R(and_6_out), .S(and_7_out), .Q(rsflipflop_3_q));
  RSFlipFlop rsflipflop_4 (.R(and_8_out), .S(and_9_out), .Q(rsflipflop_4_q));
  and and_10 (NibbleOut[0], rsflipflop_1_q, Enable);
  and and_11 (NibbleOut[1], rsflipflop_2_q, Enable);
  and and_12 (NibbleOut[2], rsflipflop_3_q, Enable);
  and and_13 (NibbleOut[3], rsflipflop_4_q, Enable);
  // Probe on NibbleOut

  // Notes on the sheet:
  //   Brandon Smith
  //   When Read_Write = 1 performs read, otherwise performs write
endmodule

module RAM_4_Nibble (
  input  [3:0] Data,
  input  ReadWrite,
  input  CLK,
  input  [1:0] Address,
  output [3:0] RAM_Out
);

  wire and_1_out, and_2_out, and_3_out, and_4_out, or_1_out, or_2_out, or_3_out, or_4_out, or_7_out,
       or_8_out, or_9_out, or_10_out;
  wire [3:0] a0000_nibbleout, a0001_nibbleout, a0010_nibbleout, a0011_nibbleout;

  // Probe on Address
  and and_1 (and_1_out, ~Address[1], ~Address[0]);  // AND_Gate
  and and_2 (and_2_out, ~Address[1], Address[0]);  // AND_Gate
  and and_3 (and_3_out, Address[1], ~Address[0]);  // AND_Gate
  and and_4 (and_4_out, Address[1], Address[0]);
  // Probe on Data
  Nibble a0000 (.Enable(and_1_out), .CLK(CLK), .ReadWrite(ReadWrite), .Data(Data), .NibbleOut(a0000_nibbleout));
  Nibble a0001 (.Enable(and_2_out), .CLK(CLK), .ReadWrite(ReadWrite), .Data(Data), .NibbleOut(a0001_nibbleout));
  Nibble a0010 (.Enable(and_3_out), .CLK(CLK), .ReadWrite(ReadWrite), .Data(Data), .NibbleOut(a0010_nibbleout));
  Nibble a0011 (.Enable(and_4_out), .CLK(CLK), .ReadWrite(ReadWrite), .Data(Data), .NibbleOut(a0011_nibbleout));
  or or_1 (or_1_out, a0001_nibbleout[2], a0000_nibbleout[2]);
  or or_2 (or_2_out, a0001_nibbleout[3], a0000_nibbleout[3]);
  or or_3 (or_3_out, a0010_nibbleout[2], or_1_out);
  or or_4 (or_4_out, a0010_nibbleout[3], or_2_out);
  or or_5 (RAM_Out[3], a0011_nibbleout[3], or_4_out);
  or or_6 (RAM_Out[2], a0011_nibbleout[2], or_3_out);
  or or_7 (or_7_out, a0001_nibbleout[1], a0000_nibbleout[1]);
  or or_8 (or_8_out, a0001_nibbleout[0], a0000_nibbleout[0]);
  or or_9 (or_9_out, a0010_nibbleout[1], or_7_out);
  or or_10 (or_10_out, a0010_nibbleout[0], or_8_out);
  or or_11 (RAM_Out[1], a0011_nibbleout[1], or_9_out);
  or or_12 (RAM_Out[0], a0011_nibbleout[0], or_10_out);
  // Probe on RAM_Out

  // Notes on the sheet:
  //   Brandon Smith
endmodule

module Register_Nibble (
  input  [3:0] Data_In,
  input  Register_Reset,
  input  CLK,
  input  Addressing,
  input  ReadWrite,
  output [3:0] Data_Out
);

  wire and_1_out, and_2_out, and_3_out, and_4_out, and_5_out, and_6_out, and_7_out, and_8_out, and_9_out,
       not_1_out, not_2_out, not_3_out, not_4_out, or_1_out, or_2_out, or_3_out, or_4_out;

  // Probe on Data_In
  not not_1 (not_1_out, Data_In[0]);
  and and_1 (and_1_out, not_1_out, and_9_out);
  and and_2 (and_2_out, Data_In[0], and_9_out);
  not not_2 (not_2_out, Data_In[1]);
  and and_3 (and_3_out, not_2_out, and_9_out);
  and and_4 (and_4_out, Data_In[1], and_9_out);
  not not_3 (not_3_out, Data_In[2]);
  and and_5 (and_5_out, not_3_out, and_9_out);
  and and_6 (and_6_out, Data_In[2], and_9_out);
  not not_4 (not_4_out, Data_In[3]);
  and and_7 (and_7_out, not_4_out, and_9_out);
  and and_8 (and_8_out, Data_In[3], and_9_out);
  and and_9 (and_9_out, Addressing, CLK, ReadWrite);
  or or_1 (or_1_out, Register_Reset, and_1_out);
  or or_2 (or_2_out, Register_Reset, and_3_out);
  or or_3 (or_3_out, Register_Reset, and_5_out);
  or or_4 (or_4_out, Register_Reset, and_7_out);
  RSFlipFlop rsflipflop_1 (.R(or_1_out), .S(and_2_out), .Q(Data_Out[0]));
  RSFlipFlop rsflipflop_2 (.R(or_2_out), .S(and_4_out), .Q(Data_Out[1]));
  RSFlipFlop rsflipflop_3 (.R(or_3_out), .S(and_6_out), .Q(Data_Out[2]));
  RSFlipFlop rsflipflop_4 (.R(or_4_out), .S(and_8_out), .Q(Data_Out[3]));
  // Probe on Data_Out

  // Notes on the sheet:
  //   Brandon Smith
endmodule

module Register_2bit (
  input  [1:0] Data_In,
  input  CLK,
  input  Addressing,
  input  ReadWrite,
  output [1:0] Data_Out
);

  wire and_1_out, and_2_out, and_3_out, and_4_out, and_5_out, and_6_out, not_1_out, not_2_out,
       rsflipflop_1_q, rsflipflop_2_q;

  // Probe on Data_In
  not not_1 (not_1_out, Data_In[0]);
  and and_1 (and_1_out, not_1_out, and_5_out);
  and and_2 (and_2_out, Data_In[0], and_5_out);
  not not_2 (not_2_out, Data_In[1]);
  and and_3 (and_3_out, not_2_out, and_5_out);
  and and_4 (and_4_out, Data_In[1], and_5_out);
  and and_5 (and_5_out, Addressing, CLK, ReadWrite);
  RSFlipFlop rsflipflop_1 (.R(and_1_out), .S(and_2_out), .Q(rsflipflop_1_q));
  RSFlipFlop rsflipflop_2 (.R(and_3_out), .S(and_4_out), .Q(rsflipflop_2_q));
  and and_6 (and_6_out, CLK, Addressing);
  // Probe on Data_Out
  and and_7 (Data_Out[0], rsflipflop_1_q, and_6_out);
  and and_8 (Data_Out[1], rsflipflop_2_q, and_6_out);

  // Notes on the sheet:
  //   Brandon Smith
endmodule

module Incrementer (
  input  [1:0] Inc_In,
  output [1:0] Inc_Out
);

  wire add_1bit_1_cout, not_1_out;

  Add_1Bit add_1bit_1 (.A(Inc_In[0]), .B(1'b1), .Cout(add_1bit_1_cout), .Sum(Inc_Out[0]));  // open: Cin
  not not_1 (not_1_out, 1'b1);
  Add_1Bit add_1bit_2 (.Cin(add_1bit_1_cout), .A(Inc_In[1]), .B(not_1_out), .Sum(Inc_Out[1]));  // open: Cout

  // Notes on the sheet:
  //   Brandon Smith
endmodule

module InstructionControlUnit (
  input  [3:0] IR_In,
  input  MicroStep,
  input  Addressing,
  output LR_Addressing,
  output LR_ReadWrite,
  output Aout_Addressing,
  output Aout_ReadWrite,
  output Status_ReadWrite,
  output RAM_ReadWrite,
  output STOP_Out
);

  wire and_1_out, and_2_out, and_3_out, and_4_out, and_5_out, and_6_out, and_7_out, and_8_out, and_9_out,
       and_10_out, and_11_out, and_12_out, and_13_out, and_14_out, and_15_out, and_16_out, and_17_out,
       and_18_out, and_19_out, and_20_out, and_21_out, and_22_out, and_23_out, and_24_out, and_25_out,
       and_26_out, and_27_out, and_28_out, and_29_out, and_30_out, and_31_out, and_32_out, not_1_out,
       not_2_out, not_3_out, not_4_out, not_5_out, or_1_out, or_2_out, or_3_out, or_4_out;

  not not_1 (not_1_out, IR_In[3]);
  not not_2 (not_2_out, IR_In[1]);
  not not_3 (not_3_out, IR_In[2]);
  not not_4 (not_4_out, MicroStep);
  not not_5 (not_5_out, IR_In[0]);
  and and_1 (and_1_out, not_1_out, not_3_out, not_2_out, not_5_out, not_4_out);
  and and_2 (and_2_out, not_1_out, not_3_out, not_2_out, not_5_out, MicroStep);
  and and_3 (and_3_out, not_1_out, not_3_out, not_2_out, IR_In[0], not_4_out);
  and and_4 (and_4_out, not_1_out, not_3_out, not_2_out, IR_In[0], MicroStep);
  and and_5 (and_5_out, not_1_out, not_3_out, IR_In[1], not_5_out, not_4_out);
  and and_6 (and_6_out, not_1_out, not_3_out, IR_In[1], not_5_out, MicroStep);
  and and_7 (and_7_out, not_1_out, not_3_out, IR_In[1], IR_In[0], not_4_out);
  and and_8 (and_8_out, not_1_out, not_3_out, IR_In[1], IR_In[0], MicroStep);
  and and_9 (and_9_out, not_1_out, IR_In[2], not_2_out, not_5_out, not_4_out);
  and and_10 (and_10_out, not_1_out, IR_In[2], not_2_out, not_5_out, MicroStep);
  and and_11 (and_11_out, not_1_out, IR_In[2], not_2_out, IR_In[0], not_4_out);
  and and_12 (and_12_out, not_1_out, IR_In[2], not_2_out, IR_In[0], MicroStep);
  and and_13 (and_13_out, not_1_out, IR_In[2], IR_In[1], not_5_out, not_4_out);
  and and_14 (and_14_out, not_1_out, IR_In[2], IR_In[1], not_5_out, MicroStep);
  and and_15 (and_15_out, not_1_out, IR_In[2], IR_In[1], IR_In[0], not_4_out);
  and and_16 (and_16_out, not_1_out, IR_In[2], IR_In[1], IR_In[0], MicroStep);
  and and_17 (and_17_out, IR_In[3], not_3_out, not_2_out, not_5_out, not_4_out);
  and and_18 (and_18_out, IR_In[3], not_3_out, not_2_out, not_5_out, MicroStep);
  and and_19 (and_19_out, IR_In[3], not_3_out, not_2_out, IR_In[0], not_4_out);
  and and_20 (and_20_out, IR_In[3], not_3_out, not_2_out, IR_In[0], MicroStep);
  and and_21 (and_21_out, IR_In[3], not_3_out, IR_In[1], not_5_out, not_4_out);
  and and_22 (and_22_out, IR_In[3], not_3_out, IR_In[1], not_5_out, MicroStep);
  and and_23 (and_23_out, IR_In[3], not_3_out, IR_In[1], IR_In[0], not_4_out);
  and and_24 (and_24_out, IR_In[3], not_3_out, IR_In[1], IR_In[0], MicroStep);
  and and_25 (and_25_out, IR_In[3], IR_In[2], not_2_out, not_5_out, not_4_out);
  and and_26 (and_26_out, IR_In[3], IR_In[2], not_2_out, not_5_out, MicroStep);
  and and_27 (and_27_out, IR_In[3], IR_In[2], not_2_out, IR_In[0], not_4_out);
  and and_28 (and_28_out, IR_In[3], IR_In[2], not_2_out, IR_In[0], MicroStep);
  and and_29 (and_29_out, IR_In[3], IR_In[2], IR_In[1], not_5_out, not_4_out);
  and and_30 (and_30_out, IR_In[3], IR_In[2], IR_In[1], not_5_out, MicroStep);
  and and_31 (and_31_out, IR_In[3], IR_In[2], IR_In[1], IR_In[0], not_4_out);
  and and_32 (and_32_out, IR_In[3], IR_In[2], IR_In[1], IR_In[0], MicroStep);
  or or_1 (or_1_out, and_3_out, and_5_out, and_7_out, and_9_out, and_11_out, and_13_out, and_15_out);
  or or_2 (or_2_out, and_4_out, and_6_out, and_8_out, and_10_out, and_12_out, and_14_out, and_16_out);
  or or_3 (or_3_out, and_17_out, and_18_out, and_19_out, and_20_out, and_21_out, and_22_out, and_23_out, and_24_out, and_25_out, and_26_out, and_27_out, and_28_out, and_29_out, and_30_out, and_31_out, and_32_out);
  or or_4 (or_4_out, and_1_out, and_2_out);
  and and_33 (LR_Addressing, Addressing, or_1_out);
  and and_34 (LR_ReadWrite, Addressing, or_1_out);
  and and_35 (Aout_Addressing, Addressing, or_2_out);
  and and_36 (Aout_ReadWrite, Addressing, or_2_out);
  and and_37 (Status_ReadWrite, Addressing, or_2_out);
  and and_38 (RAM_ReadWrite, Addressing, or_3_out);
  and and_39 (STOP_Out, Addressing, or_4_out);

  // Notes on the sheet:
  //   Brandon Smith
endmodule

module FetchControlUnit (
  input  CLK,
  input  [1:0] Fectch_Set,
  input  FetchCU_Override,
  output IR_Addressing,
  output IR_ReadWrite,
  output InstrCU_Addressing,
  output MicroStepOut,
  output PC_Increment
);

  wire and_1_out, and_2_out, and_3_out, and_4_out, not_1_out, or_1_out, or_2_out;
  wire [1:0] incrementer_1_inc_out, my_multiplexer_1_z, my_multiplexer_3_z, register_2bit_1_data_out,
       register_2bit_2_data_out;

  not not_1 (not_1_out, CLK);
  or or_1 (or_1_out, CLK, FetchCU_Override);
  My_Multiplexer my_multiplexer_1 (
    .x_0(register_2bit_2_data_out[0]), .x_1(Fectch_Set[0]), .y(FetchCU_Override), .z(my_multiplexer_1_z[0]));
  My_Multiplexer my_multiplexer_2 (
    .x_0(register_2bit_2_data_out[1]), .x_1(Fectch_Set[1]), .y(FetchCU_Override), .z(my_multiplexer_1_z[1]));
  Register_2bit register_2bit_1 (
    .Data_In(my_multiplexer_1_z), .CLK(1'b1), .Addressing(1'b1), .ReadWrite(not_1_out),
    .Data_Out(register_2bit_1_data_out));
  Register_2bit register_2bit_2 (
    .Data_In(my_multiplexer_3_z), .CLK(1'b1), .Addressing(1'b1), .ReadWrite(or_1_out),
    .Data_Out(register_2bit_2_data_out));
  My_Multiplexer my_multiplexer_3 (
    .x_0(incrementer_1_inc_out[0]), .x_1(Fectch_Set[0]), .y(FetchCU_Override), .z(my_multiplexer_3_z[0]));
  My_Multiplexer my_multiplexer_4 (
    .x_0(incrementer_1_inc_out[1]), .x_1(Fectch_Set[1]), .y(FetchCU_Override), .z(my_multiplexer_3_z[1]));
  Incrementer incrementer_1 (.Inc_In(register_2bit_1_data_out), .Inc_Out(incrementer_1_inc_out));
  and and_1 (and_1_out, ~register_2bit_1_data_out[0], ~register_2bit_1_data_out[1]);  // AND_Gate
  and and_2 (and_2_out, register_2bit_1_data_out[0], ~register_2bit_1_data_out[1]);  // AND_Gate
  and and_3 (and_3_out, ~register_2bit_1_data_out[0], register_2bit_1_data_out[1]);  // AND_Gate
  and and_4 (and_4_out, register_2bit_1_data_out[0], register_2bit_1_data_out[1]);
  or or_2 (or_2_out, and_2_out, and_3_out);
  and and_5 (IR_Addressing, CLK, and_1_out);
  and and_6 (IR_ReadWrite, CLK, and_1_out);
  and and_7 (InstrCU_Addressing, CLK, or_2_out);
  and and_8 (MicroStepOut, CLK, and_3_out);
  and and_9 (PC_Increment, CLK, and_4_out);

  // Notes on the sheet:
  //   Brandon Smith
endmodule
